# Fritzing sketch электрическая схема лимонадного автомата (saved by Fritzing 0.9.5d)
breadboards: 2

parts:
  Компонент1 = Arduino Mega 2560 (Rev3)
  M1 = fc-51 [package=THT]
  M2 = fc-51 [package=THT]
  M3 = fc-51 [package=THT]
  M5 = Stepper Motor - Bipolar
  U3 = LIPO-2000mAh [package=lipo-2000]
  U4 = LIPO-2000mAh [package=lipo-2000]
  M6 = Stepper Motor - Bipolar
  U5 = LIPO-2000mAh [package=lipo-2000]
  U6 = LIPO-2000mAh [package=lipo-2000]
  L298N2 = L298N DC motor driver
  L298N3 = L298N DC motor driver
  M7 = fc-51 [package=THT]
  VALVE1 = Plastic Solenoid Valve
  VALVE2 = Plastic Solenoid Valve
  VALVE3 = Plastic Solenoid Valve
  S1 = Water Pump [part_number=12V package=Pump]  # not connected
  S2 = Water Pump [part_number=12V package=Pump]  # not connected
  S3 = Water Pump [part_number=12V package=Pump]  # not connected
  Q1 = MOSFET-NCHANNEL [package=to220v]
  Q2 = MOSFET-NCHANNEL [package=to220v]
  Q3 = MOSFET-NCHANNEL [package=to220v]
  R1 = Resistor [tolerance=±5% resistance=220 package="0805 [SMD]"]
  R2 = Resistor [tolerance=±5% resistance=220 package="0805 [SMD]"]
  R3 = Resistor [tolerance=±5% resistance=220 package="0805 [SMD]"]
  VCC1 = Battery block 9V
  R4 = Resistor [tolerance=±5% resistance=220 package="0805 [SMD]"]
  R5 = Resistor [tolerance=±5% resistance=220 package="0805 [SMD]"]
  R6 = Resistor [tolerance=±5% resistance=220 package="0805 [SMD]"]
  S4 = Pushbutton [package="[THT]"]
  S5 = Pushbutton [package="[THT]"]
  S6 = Pushbutton [package="[THT]"]
  S7 = Pushbutton [package="[THT]"]
  S8 = Pushbutton [package="[THT]"]
  S9 = Pushbutton [package="[THT]"]
  S10 = Pushbutton [package="[THT]"]
  S11 = Pushbutton [package="[THT]"]

nets:
  N1: Компонент1.D21/SCL, M7.pin1
  N2: Компонент1.D20/SDA, M1.pin1
  N3: Компонент1.D19/RX1, M2.pin1
  N4: Компонент1.D18/TX1, M3.pin1
  N5: Компонент1.D17_PWM/RX2, S5.Pin_3, S5.Pin_4
  N6: Компонент1.D16_PWM/TX2, S6.Pin_3, S6.Pin_4
  N7: Компонент1.D15/RX3, S7.Pin_3, S7.Pin_4
  N8: Компонент1.D14/TX3, S8.Pin_3, S8.Pin_4
  GND: Компонент1.GND, M1.pin2, M2.pin2, M3.pin2, U3.-, L298N2.GND, M7.pin2, Q1.S, Q2.S, Q3.S, R1.Pin_1, R2.Pin_1, R3.Pin_1, S4.Pin_1, S4.Pin_2, S5.Pin_1, S5.Pin_2, S6.Pin_1, S6.Pin_2, S7.Pin_1, S7.Pin_2, S8.Pin_1, S8.Pin_2, S9.Pin_1, S9.Pin_2, S10.Pin_1, S10.Pin_2, S11.Pin_1, S11.Pin_2
  N9: Компонент1.D13_PWM, S11.Pin_3, S11.Pin_4
  N10: Компонент1.D12_PWM, S10.Pin_3, S10.Pin_4
  N11: Компонент1.D11_PWM, S9.Pin_3, S9.Pin_4
  N12: Компонент1.D10_PWM, R5.Pin_0
  N13: Компонент1.D9_PWM, R4.Pin_0
  N14: Компонент1.D8_PWM, R6.Pin_0
  N15: Компонент1.5V, M1.pin3, M2.pin3, M3.pin3, M7.pin3
  VIN: Компонент1.VIN, U4.+, L298N2.12V
  N16: Компонент1.D0_RX0, L298N2.IN1
  N17: Компонент1.D1_TX0, L298N2.IN2
  N18: Компонент1.D2_PWM, L298N2.IN3
  N19: Компонент1.D3_PWM, L298N2.IN4
  N20: Компонент1.D4_PWM, L298N3.IN1
  N21: Компонент1.D5_PWM, L298N3.IN2
  N22: Компонент1.D6_PWM, L298N3.IN3
  N23: Компонент1.D7_PWM, L298N3.IN4
  N24: Компонент1.D22, S4.Pin_3, S4.Pin_4
  N25: M5.A, L298N2.OUT1
  N26: M5.C, L298N2.OUT2
  N27: M5.B, L298N2.OUT3
  N28: M5.D, L298N2.OUT4
  N29: U3.+, U4.-
  N30: M6.A, L298N3.OUT1
  N31: M6.C, L298N3.OUT2
  N32: M6.B, L298N3.OUT3
  N33: M6.D, L298N3.OUT4
  N34: U5.+, U6.-
  N35: U5.-, L298N3.GND
  N36: U6.+, L298N3.12V
  N37: VALVE1.no_name_yet#1, VALVE2.no_name_yet#1, VALVE3.no_name_yet#1, VCC1.+
  N38: VALVE1.no_name_yet#2, Q1.D
  N39: VALVE2.no_name_yet#2, Q3.D
  N40: VALVE3.no_name_yet#2, Q2.D
  N41: Q1.G, R1.Pin_0, R6.Pin_1
  N42: Q2.G, R2.Pin_0, R5.Pin_1
  N43: Q3.G, R3.Pin_0, R4.Pin_1

custom parts:
  L298N DC motor driver: 2x DC motor driver with 78M05 positive voltage regulator (7..35 V) L298N: max 46 V, 2 A Set 5 V Enable jumper to enable 5 V regultor (needed for the L298N) and +5 V output at screw terminal or supply external +5 V at screw terminal Set ENA and/or ENB to +5 V to enable motor permanently or supply ENA and/or ENB with PWM signal IN1 and IN2 set rotation directory for motor A (OUT1/OUT2) IN2 and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
  Water Pump: A Water Pump DC 12V
